# Fritzing sketch Spidy (saved by Fritzing 0.9.3b)

parts:
  MCU1 = Raspberry Pi Zero
  PWM1 = PCA9685 16x12-bit PWM Breakout
  J1 = Basic Servo

nets:
  N1: MCU1.pin_1, MCU1.pin_17, PWM1.no_name_yet#505
  N2: MCU1.pin_3, PWM1.no_name_yet#504
  N3: MCU1.pin_5, PWM1.no_name_yet#503
  N4: MCU1.pin_6, MCU1.pin_9
  N5: PWM1.no_name_yet#0, J1.pulse
  N6: PWM1.no_name_yet#100, PWM1.no_name_yet#706, J1.vcc
  N7: PWM1.no_name_yet#501, PWM1.no_name_yet#701, PWM1.no_name_yet#1000, J1.gnd

notes:
  * 12 Servos
  Pin# 06 blau GND
  Pin# 01 rot 3,3 Volt
  Pin# 03 orange SDA I2C
  Pin# 05 gelb SCL I2C
  Pin# 09 grün *OE Out Enable bei Low
  Max 5,5 Volt
  Strom > 2A
